# Fritzing sketch Diagram (saved by Fritzing 0.8.7b)
breadboards: 1

parts:
  Teensy1 = Teensy 4.1
  Left_Side = HC-SR501 Body Sensor Module
  Right_Side = HC-SR501 Body Sensor Module
  ^_SQM_Front_^ = LM35 Temperature Sensor [package="TO92 [THT]"]
  Part1 = Adafruit TCS34725 RGB Color Sensor [part_number="Adafruit #1334"]
  LED2 = LED - 5mm [color="Yellow (595nm)" package="5 mm [THT]"]
  LED3 = LED - 5mm [color="Yellow (595nm)" package="5 mm [THT]"]
  LED4 = LED - 5mm [color="Yellow (595nm)" package="5 mm [THT]"]
  LED5 = LED - 5mm [color="Yellow (595nm)" package="5 mm [THT]"]
  LED6 = LED - 5mm [color="Yellow (595nm)" package="5 mm [THT]"]
  LED7 = LED - 5mm [color="Yellow (595nm)" package="5 mm [THT]"]

nets:
  GND: Teensy1.GND, Teensy1.GND2#55, Left_Side.GND, Right_Side.GND, ^_SQM_Front_^.+Vs, Part1.GND, Part1.LED_EN, LED2.cathode, LED3.cathode, LED4.cathode, LED5.cathode, LED6.cathode, LED7.cathode
  N1: Teensy1.D5, Left_Side.OUT
  N2: Teensy1.D6, Right_Side.OUT
  N3: Teensy1.D13, LED2.anode, LED3.anode, LED4.anode
  N4: Teensy1.A0/D14, ^_SQM_Front_^.GND
  N5: Teensy1.A1/D15, LED5.anode, LED6.anode, LED7.anode
  N6: Teensy1.A4/D18, Part1.SDA
  N7: Teensy1.A5/D19, Part1.SCL
  N8: Teensy1.3V3_LOW, ^_SQM_Front_^.Vout, Part1.+3V3
  VCC: Teensy1.Vin, Left_Side.VCC, Right_Side.VCC

custom parts:
  Teensy 4.1: The Teensy is a complete USB-based microcontoller development system, in a very small footprint, capable of implementing many types of projects. All programming is done via the USB port. No special programmer is needed, only a standard micro-USB cable and a PC or Macintosh with a USB port.
  HC-SR501 Body Sensor Module: Pyroelectric Infrared PIR Motion Sensor Detector Module
  Adafruit TCS34725 RGB Color Sensor: Your electronics can now see in dazzling color with this lovely color light sensor. We found the best color sensor on the market, the TCS34725, which has RGB and Clear light sensing elements. An IR blocking filter, integrated on-chip and localized to the color sensing photodiodes, minimizes the IR spectral component of the incoming light and allows color measurements to be made accurately. The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
